# Fritzing sketch esp32-power-meter (saved by Fritzing 0.9.6b)

parts:
  R1 = Resistor [tolerance=±5% power=0.25 resistance=470k package=THT]
  LTR_1 = Monacor line transformer [part_number=LTR-110]
  R2 = Resistor [tolerance=±5% power=0.25 resistance=5.6k package=THT]
  R3 = Resistor [tolerance=±5% power=0.25 resistance=33k package=THT]
  R5 = Resistor [tolerance=±5% power=0.25 resistance=27 package=THT]
  C4 = Capacitor [part_number=10uF package=cap-pth-small2]
  R6 = Resistor [tolerance=±5% power=0.25 resistance=10k package=THT]
  R7 = Resistor [tolerance=±5% power=0.25 resistance=27 package=THT]
  MH-ET_Live_Minikit_for_ESP1 = MH-ET Live Minikit for ESP32
  J1 = Dagu DGServo 9g header connector (female) [package=THT]

nets:
  N1: R1.Pin_0, R6.Pin_0, MH-ET_Live_Minikit_for_ESP1.IO34
  N2: R1.Pin_1, LTR_1.GND
  N3: LTR_1.08, R2.Pin_0, R3.Pin_0, C4.2, R6.Pin_1, R7.Pin_0, J1.gnd
  N4: R2.Pin_1, C4.1, MH-ET_Live_Minikit_for_ESP1.GND
  N5: R3.Pin_1, MH-ET_Live_Minikit_for_ESP1.3.3V
  N6: R5.Pin_0, MH-ET_Live_Minikit_for_ESP1.IO35, J1.pulse
  N7: R7.Pin_1, MH-ET_Live_Minikit_for_ESP1.SVN, J1.Vcc

notes:
  Current Clamp 1
  Common
  Current Clamp 2
  220V - 24V
  AC Transformer

custom parts:
  MH-ET Live Minikit for ESP32: MH-ET Live Minikit for ESP32 ( http://mh.nodebb.com/topic/8/mh-et-live-minikit-for-esp32/2/) PCB footprint is invalid.
